# Fritzing sketch breathing_belt_arduino_connection (saved by Fritzing 0.7.0b)
breadboards: 1

parts:
  Arduino1 = Arduino
  U1 = mystery part, 3 pins [chip_label="trimmer 3386 resistor" spacing=300mil]
  U2 = mystery part, 3 pins [chip_label="trimmer 3386 resistor" spacing=300mil]
  R1 = Resistor [tolerance=±5% resistance=220 package=THT]

nets:
  N1: Arduino1.aref, U1.pin2, U2.pin1
  N2: Arduino1.3V3, U1.pin1
  N3: Arduino1.A0, R1.Pin_1

notes:
  Arduino USB plugged
  2 potentiometers: Trimmer 3386,
  100 & 200 Ohms.
  https://abra-electronics.com/potentiometers/3386f-series-1-2w-single-turn-cermet-square/3386f-1-201-single-turn-cermet-potentiometer-200-ohms-3386f-1-201.html
  1 resistor
  2 inputs to the breathing belt
